// Logisim project s-mips.circ as structural Verilog: 13 circuits, main circuit S-MIPS Board
module S_MIPS_Board (
  input  DESHABILITAR_DISPATCHER,
  output halt
);

  wire button_1_out, CLK, CS, d_ff_1_q, LCLR, LoadRAM, LoadRAMOn, LW, R_R_W, R_W, ram_dispatcher_1_finished,
       RCS, Reset_out, RST, TTY_EN;
  wire [2:0] KDB;
  wire [3:0] LMask, Mask, ram_1_read_time, ram_1_write_time, RMask;
  wire [6:0] KDB_DATA, TTY_DATA;
  wire [15:0] Addr, LAddr, RAddr;
  wire [31:0] I0, I1, I2, I3, LData, ram_1_data_out_0, ram_1_data_out_1, ram_1_data_out_2, ram_1_data_out_3,
       RI0, RI1, RI2, RI3;

  TTY #(.rows(25), .cols(80)) tty_1 (.data(TTY_DATA), .clk(CLK), .we(TTY_EN), .clr(RST));
  not not_1 (LoadRAMOn, ram_dispatcher_1_finished);
  RAM_Dispatcher ram_dispatcher_1 (
    .WriteTime(ram_1_write_time), .Clock(CLK), .Data(LData), .Address(LAddr), .Mask(LMask),
    .Finished(ram_dispatcher_1_finished), .Write(LW), .CLR(LCLR));
  Keyboard #(.buflen(64)) keyboard_1 (.clk(CLK), .re(KDB[0]), .avail(KDB[2]), .data(KDB_DATA));  // open: clr
  RAM ram_1 (
    .Address(RAddr), .Data_Out_0(ram_1_data_out_0), .Data_Out_1(ram_1_data_out_1),
    .Data_Out_2(ram_1_data_out_2), .Data_Out_3(ram_1_data_out_3), .Data_In_0(RI0), .Data_In_1(RI1),
    .Data_In_2(RI2), .Data_In_3(RI3), .Mask(RMask), .nRead_Write(R_R_W), .Chip_Select(RCS),
    .Read_Time(ram_1_read_time), .Reset(button_1_out), .Write_Time(ram_1_write_time));
  Button button_1 (.out(button_1_out));
  D_Flip_Flop d_ff_1 (.clk(CLK), .D(1'b1), .Q(d_ff_1_q), .reset(Reset_out));  // open: Qn, preset, en
  Button Reset (.out(Reset_out));
  S_MIPS s_mips_1 (
    .Kbd_Enable(KDB[0]), .Address(Addr), .Kbd_Clear(KDB[1]), .Kbd_Available(KDB[2]), .RAM_In_0(I0),
    .Kbd_ASCII_Data(KDB_DATA), .RAM_In_1(I1), .TTY_Enable(TTY_EN), .RAM_In_2(I2), .RAM_In_3(I2),
    .TTY_ASCII_Data(TTY_DATA), .Reset(RST), .RAM_Out_0(ram_1_data_out_0), .Clock(CLK),
    .RAM_Out_1(ram_1_data_out_1), .Stop(halt), .RAM_Out_2(ram_1_data_out_2), .RAM_Out_3(ram_1_data_out_3),
    .Mask(Mask), .Read_Time(ram_1_read_time), .Write_Time(ram_1_write_time), .nRead_Write(R_W),
    .Chip_Select(CS));
  D_Flip_Flop d_ff_2 (.clk(CLK), .D(d_ff_1_q), .Qn(LCLR), .reset(Reset_out));  // open: Q, preset, en
  or or_1 (RST, LCLR, LoadRAM);
  Clock clock_1 (.out(CLK));
  Multiplexer #(.width(32), .enable("false")) multiplexer_1 (.in0(I0), .in1(LData), .out(RI0), .sel(LoadRAM));
  Multiplexer #(.width(32), .enable("false")) multiplexer_2 (.in0(I1), .in1(LData), .out(RI1), .sel(LoadRAM));
  Multiplexer #(.width(32), .enable("false")) multiplexer_3 (.in0(I2), .in1(LData), .out(RI2), .sel(LoadRAM));
  Multiplexer #(.width(32), .enable("false")) multiplexer_4 (.in0(I3), .in1(LData), .out(RI3), .sel(LoadRAM));
  and and_1 (LoadRAM, ~DESHABILITAR_DISPATCHER, LoadRAMOn);  // AND_Gate
  Multiplexer #(.width(16), .enable("false")) multiplexer_5 (.in0(Addr), .in1(LAddr), .out(RAddr), .sel(LoadRAM));
  Multiplexer #(.width(4), .enable("false")) multiplexer_6 (.in0(Mask), .in1(LMask), .out(RMask), .sel(LoadRAM));
  Multiplexer #(.enable("false")) multiplexer_7 (.in0(CS), .in1(LW), .out(RCS), .sel(LoadRAM));
  Multiplexer #(.enable("false")) multiplexer_8 (.in0(R_W), .in1(LW), .out(R_R_W), .sel(LoadRAM));

  // Notes on the sheet:
  //   NO MODIFICAR
  //   Keyboard
endmodule

module RAM (
  input  [15:0] Address,
  input  [31:0] Data_In_0,
  input  [31:0] Data_In_1,
  input  [31:0] Data_In_2,
  input  [31:0] Data_In_3,
  input  [3:0] Mask,
  input  nRead_Write,
  input  Chip_Select,
  input  Reset,
  output [31:0] Data_Out_0,
  output [31:0] Data_Out_1,
  output [31:0] Data_Out_2,
  output [31:0] Data_Out_3,
  output [3:0] Read_Time,
  output [3:0] Write_Time
);

  wire and_2_out, and_3_out, and_4_out, and_5_out, and_6_out, and_7_out, and_8_out, and_9_out, Changed, CLK,
       comparator_2_eq, comparator_3_eq, comparator_4_eq, comparator_5_eq, comparator_6_eq, Count,
       demultiplexer_3_out0, Idle, Idle_q, Load, Load0, Load1, nand_1_out, or_1_out, or_2_out, or_3_out,
       or_4_out, or_5_out, or_6_out, or_7_out, or_8_out, or_9_out, or_10_out, Proc_q, Update_Mem, Zero_Time;
  wire [3:0] counter_1_q, multiplexer_1_out, subtractor_1_out;
  wire [31:0] register_1_q, register_2_q, register_3_q, register_4_q, register_5_q;

  // Probe on 4'b0011
  // Probe on 4'b0010
  Multiplexer #(.width(4), .enable("false")) multiplexer_1 (
    .in0(4'b0011), .in1(4'b0010), .out(multiplexer_1_out), .sel(nRead_Write));
  or or_1 (or_1_out, Idle, Update_Mem);
  or or_2 (or_2_out, ~Chip_Select, Reset);  // OR_Gate
  Subtractor #(.width(4)) subtractor_1 (.a(multiplexer_1_out), .b(4'b0010), .out(subtractor_1_out));  // open: bin, bout
  D_Flip_Flop u_Idle (.clk(CLK), .D(or_1_out), .Q(Idle_q), .preset(or_2_out));  // open: Qn, en, reset
  Demultiplexer #(.enable("false")) demultiplexer_1 (.out0(Idle), .out1(Load0), .in(Idle_q), .sel(Changed));
  // Probe on counter_1_q
  Counter #(.width(4), .max('hf)) counter_1 (
    .load(Load), .D(subtractor_1_out), .count(Count), .Q(counter_1_q), .clk(CLK), .clr(or_3_out));  // open: carry
  or or_3 (or_3_out, ~Chip_Select, Reset);  // OR_Gate
  Comparator #(.width(4), .mode("unsigned")) comparator_1 (
    .a(4'b0000), .b(counter_1_q), .eq(Zero_Time));  // open: gt, lt
  or or_4 (or_4_out, Count, Load0, Load1);
  Register #(.width(32)) register_1 (.D(Data_In_0), .en(Chip_Select), .Q(register_1_q), .clk(CLK), .clr(or_5_out));
  or or_5 (or_5_out, ~Chip_Select, Reset);  // OR_Gate
  Register #(.width(32)) register_2 (.D(Data_In_1), .en(Chip_Select), .Q(register_2_q), .clk(CLK), .clr(or_6_out));
  or or_6 (or_6_out, ~Chip_Select, Reset);  // OR_Gate
  Register #(.width(32)) register_3 (.D(Data_In_2), .en(Chip_Select), .Q(register_3_q), .clk(CLK), .clr(or_7_out));
  or or_7 (or_7_out, ~Chip_Select, Reset);  // OR_Gate
  Register #(.width(32)) register_4 (.D(Data_In_3), .en(Chip_Select), .Q(register_4_q), .clk(CLK), .clr(or_8_out));
  or or_8 (or_8_out, ~Chip_Select, Reset);  // OR_Gate
  Register #(.width(32)) register_5 (
    .D({{11{1'b1}}, nRead_Write, Mask, Address}), .en(Chip_Select), .Q(register_5_q), .clk(CLK),
    .clr(or_9_out));
  or or_9 (or_9_out, ~Chip_Select, Reset);  // OR_Gate
  D_Flip_Flop Proc (.clk(CLK), .D(or_4_out), .Q(Proc_q), .reset(or_10_out));  // open: Qn, preset, en
  or or_10 (or_10_out, ~Chip_Select, Reset);  // OR_Gate
  Demultiplexer #(.enable("false")) demultiplexer_2 (
    .out0(Count), .out1(Update_Mem), .in(demultiplexer_3_out0), .sel(Zero_Time));
  Demultiplexer #(.enable("false")) demultiplexer_3 (
    .out0(demultiplexer_3_out0), .out1(Load1), .in(Proc_q), .sel(Changed));
  Clock clock_1 (.out(CLK));
  Comparator #(.width(32)) comparator_2 (.a(register_1_q), .b(Data_In_0), .eq(comparator_2_eq));  // open: gt, lt
  Comparator #(.width(32)) comparator_3 (.a(register_2_q), .b(Data_In_1), .eq(comparator_3_eq));  // open: gt, lt
  Comparator #(.width(32)) comparator_4 (.a(register_3_q), .b(Data_In_2), .eq(comparator_4_eq));  // open: gt, lt
  Comparator #(.width(32)) comparator_5 (.a(register_4_q), .b(Data_In_3), .eq(comparator_5_eq));  // open: gt, lt
  Comparator #(.width(32)) comparator_6 (
    .a(register_5_q), .b({{11{1'b1}}, nRead_Write, Mask, Address}), .eq(comparator_6_eq));  // open: gt, lt
  nand nand_1 (nand_1_out, comparator_6_eq, comparator_2_eq, comparator_3_eq, comparator_4_eq, comparator_5_eq);
  and and_1 (Changed, nand_1_out, Chip_Select);
  or or_11 (Load, Count, Load1, Load0);
  and and_2 (and_2_out, Mask[0], Update_Mem, nRead_Write);
  and and_3 (and_3_out, Mask[1], Update_Mem, nRead_Write);
  and and_4 (and_4_out, Mask[2], Update_Mem, nRead_Write);
  and and_5 (and_5_out, Mask[3], Update_Mem, nRead_Write);
  RAM_part #(.addrWidth(16), .dataWidth(32), .bus("separate")) ram_1 (
    .addr(Address), .din(Data_In_0), .data(Data_Out_0), .str(and_2_out), .sel(Chip_Select), .clk(CLK),
    .ld(and_6_out), .clr(Reset));
  and and_6 (and_6_out, ~nRead_Write, Idle);  // AND_Gate
  RAM_part #(.addrWidth(16), .dataWidth(32), .bus("separate")) ram_2 (
    .addr(Address), .din(Data_In_1), .data(Data_Out_1), .str(and_3_out), .sel(Chip_Select), .clk(CLK),
    .ld(and_7_out), .clr(Reset));
  and and_7 (and_7_out, ~nRead_Write, Idle);  // AND_Gate
  RAM_part #(.addrWidth(16), .dataWidth(32), .bus("separate")) ram_3 (
    .addr(Address), .din(Data_In_2), .data(Data_Out_2), .str(and_4_out), .sel(Chip_Select), .clk(CLK),
    .ld(and_8_out), .clr(Reset));
  and and_8 (and_8_out, ~nRead_Write, Idle);  // AND_Gate
  RAM_part #(.addrWidth(16), .dataWidth(32), .bus("separate")) ram_4 (
    .addr(Address), .din(Data_In_3), .data(Data_Out_3), .str(and_5_out), .sel(Chip_Select), .clk(CLK),
    .ld(and_9_out), .clr(Reset));
  and and_9 (and_9_out, ~nRead_Write, Idle);  // AND_Gate

  assign Read_Time = 4'b0011;
  assign Write_Time = 4'b0010;

  // Other names for the same wires on the sheet: M0 = Mask[0]; M1 = Mask[1]; M2 = Mask[2]; M3 = Mask[3];
  //   RW = nRead_Write; CLR = Reset; CS = Chip_Select; Load2 = Count

  // Notes on the sheet:
  //   NO MODIFICAR
  //   excepto quizás los valores RT y WT
  //   BANK0
  //   BANK1
  //   BANK2
  //   BANK3
endmodule

module S_MIPS (
  input  Kbd_Available,
  input  [6:0] Kbd_ASCII_Data,
  input  [31:0] RAM_Out_0,
  input  [31:0] RAM_Out_1,
  input  Reset,
  input  [31:0] RAM_Out_2,
  input  [31:0] RAM_Out_3,
  input  Clock,
  input  [3:0] Read_Time,
  input  [3:0] Write_Time,
  output Kbd_Enable,
  output [15:0] Address,
  output Kbd_Clear,
  output TTY_Enable,
  output [6:0] TTY_ASCII_Data,
  output Stop,
  output [31:0] RAM_In_0,
  output [31:0] RAM_In_1,
  output [31:0] RAM_In_2,
  output [31:0] RAM_In_3,
  output [3:0] Mask,
  output nRead_Write,
  output Chip_Select
);

  wire ALU, and_3_out, and_4_out, BC, chsp, chsp0, chsp1, CLK, CS0, CS2, d_ff_2_q, d_ff_3_q, d_ff_5_q,
       demultiplexer_2_out0, demultiplexer_2_out1, demultiplexer_4_out0, demultiplexer_5_out0,
       demultiplexer_6_out0, demultiplexer_11_out0, demultiplexer_12_out0, demultiplexer_12_out1,
       demultiplexer_13_out0, demultiplexer_14_out0, FWR, GetINst, INSDECD_q, kbd, lw, lwinst, Mul_Div, NF,
       nop, nor_1_out, Op_const, or_3_out, or_4_out, or_5_out, or_7_out, or_8_out, or_9_out, or_10_out,
       or_11_out, or_12_out, or_14_out, or_17_out, or_18_out, OS, pop, push, rnd, Rw0, Rw_t, sta, sw, swinst,
       tear, tty, ttyenable, waiter_1_ouput, waiter_2_ouput, WHI, WRF, WRFIN, ZF;
  wire [1:0] FC, multiplexer_5_out, multiplexer_8_out, SRAM2;
  wire [1:1] or_2_out;
  wire [2:0] DS, Jump;
  wire [3:0] Mask1, Mask2, Mask3, multiplexer_9_out, Op;
  wire [4:0] DA, Sa, Sb;
  wire [15:0] AddrLw, Bloque, Bloque2;
  wire [31:0] adder_1_out, B, demultiplexer_3_out1, HI, Instruction, K, KBDATA, le_1_out_2, le_2_out_2, LO,
       multiplexer_2_out, multiplexer_4_out, multiplexer_7_out, PC_in, PC_out, Ram, REM, RES, RK, SP;
  wire [31:7] A;

  or or_1 (Chip_Select, CS0, CS2, nRead_Write);
  Demultiplexer #(.select(2), .enable("false")) demultiplexer_1 (
    .out0(Mask1[0]), .out1(Mask1[1]), .out2(Mask1[2]), .out3(Mask1[3]), .in(1'b1), .sel(PC_in[3:2]));
  nor nor_1 (nor_1_out, PC_in[31], PC_in[30], PC_in[29], PC_in[28], PC_in[27], PC_in[26], PC_in[25], PC_in[24], PC_in[23], PC_in[22], PC_in[21], PC_in[20], Bloque[15], Bloque[14], Bloque[13], Bloque[12], Bloque[11], Bloque[10], Bloque[9], Bloque[8], Bloque[7], Bloque[6], Bloque[5], Bloque[4], Bloque[3], Bloque[2], Bloque[1], Bloque[0], PC_in[3], PC_in[2], PC_in[1], PC_in[0]);
  INS_DEC ins_dec_1 (
    .K(K), .Sa(Sa), .Sb(Sb), .DA(DA), .DS(DS), .Jump(Jump), .FC(FC), .OS(OS), .Mul_Div(Mul_Div),
    .Op_const(Op_const), .pop(pop), .push(push), .nop(nop), .halt(Stop), .tty(tty), .rnd(rnd), .kbd(kbd),
    .Op(Op), .alu(ALU), .wrf(WRF), .lw(lw), .sw(sw), .in_1(Instruction));
  Multiplexer #(.width(32), .enable("false")) multiplexer_1 (
    .in0({32{1'b1}}), .in1({{25{1'b0}}, Kbd_ASCII_Data}), .out(KBDATA), .sel(Kbd_Available));
  // Probe on FC
  // Probe on OS
  // Probe on Jump
  Register #(.width(32)) PC (.D(PC_out), .Q({PC_in[31:20], Bloque, PC_in[3:0]}), .clk(BC), .clr(Reset));  // open: en
  Multiplexer #(.width(32), .enable("false")) multiplexer_2 (.in0(B), .in1(K), .out(multiplexer_2_out), .sel(Op_const));
  // Probe on Op
  or or_2 (or_2_out[1], pop, push);
  Multiplexer #(.select(2), .width(16), .enable("false")) multiplexer_3 (
    .in0(AddrLw), .in1(Bloque), .in2(Bloque2), .out(Address), .sel({or_2_out[1], GetINst}));  // open: in3
  Multiplexer #(.select(2), .width(32), .enable("false")) multiplexer_4 (
    .in0(RAM_Out_0), .in1(RAM_Out_1), .in2(RAM_Out_2), .in3(RAM_Out_3), .out(multiplexer_4_out),
    .sel(multiplexer_5_out));
  Multiplexer #(.select(2), .width(2), .enable("false")) multiplexer_5 (
    .in0(SRAM2), .in1(PC_in[3:2]), .in2(SP[3:2]), .out(multiplexer_5_out), .sel({pop, GetINst}));  // open: in3
  or or_3 (or_3_out, CS0, nor_1_out, BC);
  // Probe on {PC_in[31:20], Bloque, PC_in[3:0]}
  ALU alu_1 (
    .out_4(REM), .in_1({A, TTY_ASCII_Data}), .in_2(multiplexer_2_out), .in_3(Op), .out_6(ZF), .out_7(NF),
    .out_5(RES));
  // Probe on Ram
  // Probe on multiplexer_4_out
  and and_1 (Kbd_Enable, kbd, BC);
  and and_2 (TTY_Enable, tty, ttyenable);
  D_Flip_Flop #(.trigger("high")) Fetch (.clk(CLK), .D(or_3_out), .Q(GetINst));  // open: Qn, preset, en, reset
  Waiter waiter_1 (.CLK(CLK), .STOP(Read_Time), .Ouput(waiter_1_ouput), .Reset(or_4_out));
  or or_4 (or_4_out, BC, Reset, INSDECD_q);
  and and_3 (and_3_out, WHI, Mul_Div);
  // Probe on le_1_out_2
  LE le_1 (.Input(multiplexer_4_out), .out_2(le_1_out_2));
  Demultiplexer #(.enable("false")) demultiplexer_2 (
    .out0(demultiplexer_2_out0), .out1(demultiplexer_2_out1), .in(GetINst), .sel(waiter_1_ouput));
  Register #(.width(32)) u_LO (.D(RES), .Q(LO), .clk(and_3_out), .clr(Reset));  // open: en
  and and_4 (and_4_out, WHI, Mul_Div);
  // Probe on RES
  RegisterFile registerfile_1 (
    .in_1(RES), .in_2(RK), .in_4(Ram), .in_5(KBDATA), .in_6(HI), .in_7(LO), .in_8(push), .in_10(pop),
    .in_11(chsp), .SP({SP[31:20], Bloque2, SP[3:0]}), .out_18({A, TTY_ASCII_Data}), .out_19(B), .in_16(DA),
    .in_3(DS), .in_13(Rw_t), .in_14(CLK), .in_15(Reset), .in_9(Sa), .in_12(Sb));
  Multiplexer #(.select(2), .width(4), .enable("false")) multiplexer_6 (
    .in0(Mask2), .in1(Mask1), .in2(Mask3), .out(Mask), .sel({or_2_out[1], GetINst}));  // open: in3
  Demultiplexer #(.width(32), .enable("false")) demultiplexer_3 (
    .out0(Ram), .out1(demultiplexer_3_out1), .in(le_1_out_2), .sel(GetINst));
  D_Flip_Flop #(.trigger("falling")) d_ff_1 (
    .clk(CLK), .D(demultiplexer_2_out0), .Q(CS0));  // open: Qn, preset, en, reset
  Register #(.width(32)) u_HI (.D(REM), .Q(HI), .clk(and_4_out), .clr(Reset));  // open: en
  Adder #(.width(32)) adder_1 (
    .a(K), .b({A, TTY_ASCII_Data}), .out({adder_1_out[31:20], AddrLw, SRAM2, adder_1_out[1:0]}));  // open: cin, cout
  nor nor_2 (CLK, Clock, Stop);
  Random #(.width(32)) random_1 (.clk(CLK), .out(RK));  // open: next, clr
  // Probe on {SP[31:20], Bloque2, SP[3:0]}
  // Probe on {A, TTY_ASCII_Data}
  Register #(.width(32), .trigger("high")) register_1 (
    .D(demultiplexer_3_out1), .Q(Instruction), .clk(GetINst), .clr(Reset));  // open: en
  D_Flip_Flop #(.trigger("falling")) INSDECD (
    .clk(CLK), .D(demultiplexer_2_out1), .Q(INSDECD_q));  // open: Qn, preset, en, reset
  BC bc_1 (
    .in_1(K), .in_3({A, TTY_ASCII_Data}), .in_5({PC_in[31:20], Bloque, PC_in[3:0]}), .in_6(ZF), .in_7(NF),
    .out_9(PC_out), .in_4(Jump), .in_2(OS), .in_8(FC));
  // Probe on B
  Multiplexer #(.width(32), .enable("false")) multiplexer_7 (
    .in0({A, TTY_ASCII_Data}), .in1(B), .out(multiplexer_7_out), .sel(lw));
  Demultiplexer #(.enable("false")) demultiplexer_4 (
    .out0(demultiplexer_4_out0), .out1(lwinst), .in(demultiplexer_5_out0), .sel(lw));
  Demultiplexer #(.enable("false")) demultiplexer_5 (
    .out0(demultiplexer_5_out0), .out1(sta), .in(INSDECD_q), .sel(or_5_out));
  or or_5 (or_5_out, pop, push);
  Demultiplexer #(.enable("false")) demultiplexer_6 (.out0(demultiplexer_6_out0), .out1(chsp0), .in(sta), .sel(push));
  or or_6 (chsp, chsp0, chsp1);
  Multiplexer #(.width(2), .enable("false")) multiplexer_8 (
    .in0(SP[3:2]), .in1(SRAM2), .out(multiplexer_8_out), .sel(lw));
  LE le_2 (.Input(multiplexer_7_out), .out_2(le_2_out_2));
  Demultiplexer #(.select(2), .width(32), .enable("false")) demultiplexer_7 (
    .out0(RAM_In_0), .out1(RAM_In_1), .out2(RAM_In_2), .out3(RAM_In_3), .in(le_2_out_2),
    .sel(multiplexer_8_out));
  or or_7 (or_7_out, demultiplexer_6_out0, chsp0);
  Multiplexer #(.width(4), .enable("false")) multiplexer_9 (
    .in0(Read_Time), .in1(Write_Time), .out(multiplexer_9_out), .sel(or_8_out));
  or or_8 (or_8_out, sw, push);
  Demultiplexer #(.select(2), .enable("false")) demultiplexer_8 (
    .out0(Mask2[0]), .out1(Mask2[1]), .out2(Mask2[2]), .out3(Mask2[3]), .in(1'b1), .sel(SRAM2));
  or or_9 (or_9_out, d_ff_3_q, swinst, or_7_out, lwinst);
  or or_10 (or_10_out, tear, Reset, d_ff_5_q);
  Demultiplexer #(.enable("false")) demultiplexer_9 (.out0(WHI), .out1(WRFIN), .in(demultiplexer_4_out0), .sel(WRF));
  Demultiplexer #(.enable("false")) demultiplexer_10 (.out0(CS2), .out1(nRead_Write), .in(d_ff_2_q), .sel(or_11_out));
  D_Flip_Flop #(.trigger("high")) d_ff_2 (.clk(CLK), .D(or_9_out), .Q(d_ff_2_q));  // open: Qn, preset, en, reset
  or or_11 (or_11_out, sw, push);
  Waiter waiter_2 (.CLK(CLK), .STOP(multiplexer_9_out), .Ouput(waiter_2_ouput), .Reset(or_10_out));
  Demultiplexer #(.enable("false")) demultiplexer_11 (.out0(demultiplexer_11_out0), .out1(swinst), .in(WHI), .sel(sw));
  Demultiplexer #(.enable("false")) demultiplexer_12 (
    .out0(demultiplexer_12_out0), .out1(demultiplexer_12_out1), .in(or_12_out), .sel(waiter_2_ouput));
  or or_12 (or_12_out, CS2, nRead_Write);
  or or_13 (ttyenable, FWR, demultiplexer_11_out0, or_14_out);
  or or_14 (or_14_out, demultiplexer_13_out0, chsp1);
  D_Flip_Flop #(.trigger("falling")) d_ff_3 (
    .clk(CLK), .D(demultiplexer_12_out0), .Q(d_ff_3_q));  // open: Qn, preset, en, reset
  D_Flip_Flop #(.trigger("falling")) d_ff_4 (.clk(CLK), .D(WRFIN), .Q(FWR));  // open: Qn, preset, en, reset
  Demultiplexer #(.enable("false")) demultiplexer_13 (
    .out0(demultiplexer_13_out0), .out1(chsp1), .in(or_17_out), .sel(pop));
  D_Flip_Flop #(.trigger("falling")) d_ff_5 (
    .clk(CLK), .D(demultiplexer_12_out1), .Q(d_ff_5_q));  // open: Qn, preset, en, reset
  Demultiplexer #(.enable("false")) demultiplexer_14 (
    .out0(demultiplexer_14_out0), .out1(Rw0), .in(d_ff_5_q), .sel(or_18_out));
  or or_15 (tear, sta, lwinst, swinst);
  or or_16 (Rw_t, FWR, Rw0);
  Demultiplexer #(.select(2), .enable("false")) demultiplexer_15 (
    .out0(Mask3[0]), .out1(Mask3[1]), .out2(Mask3[2]), .out3(Mask3[3]), .in(1'b1), .sel(SP[3:2]));
  D_Flip_Flop #(.trigger("falling")) d_ff_6 (.clk(CLK), .D(ttyenable), .Q(BC));  // open: Qn, preset, en, reset
  or or_17 (or_17_out, demultiplexer_14_out0, Rw0);
  or or_18 (or_18_out, lw, pop);

  assign Kbd_Clear = Reset;

  // Other names for the same wires on the sheet: SRAM1[1:0] = PC_in[3:2]; PC_in[19:4] = Bloque;
  //   A[6:0] = TTY_ASCII_Data; TTY_DATA[6:0] = TTY_ASCII_Data; SP[19:4] = Bloque2; CS = Chip_Select; halt = Stop;
  //   KBD_AVAIL = Kbd_Available; CLR = Reset; KBD_CLR = Reset; KBD_DATA[6:0] = Kbd_ASCII_Data; FI = BC;
  //   kbdenable = BC; RAM_A[15:0] = Address; RAM_INPUT_0[31:0] = RAM_In_0; RAM_INPUT_1[31:0] = RAM_In_1;
  //   RAM_INPUT_2[31:0] = RAM_In_2; RAM_INPUT_3[31:0] = RAM_In_3; RAM_MASK[3:0] = Mask;
  //   RAM_OUTPUT_0[31:0] = RAM_Out_0; RAM_OUTPUT_1[31:0] = RAM_Out_1; RAM_OUTPUT_2[31:0] = RAM_Out_2;
  //   RAM_OUTPUT_3[31:0] = RAM_Out_3; CS3 = nRead_Write; RW = nRead_Write; Rw1 = FWR; SRAM3[1:0] = SP[3:2]; WLO = WHI

  // Notes on the sheet:
  //   RAM ADDRESS
  //   DATA FROM RAM
  //   DATA TO RAM
  //   DATA WRITE MASK
  //   RAM TIMING
  //   RAM CONTROL
  //   KEYBOARD
  //   TTY
  //   SEQUENCING
  //   RAMDOM
endmodule

module RegisterFile (
  input  [31:0] in_1,
  input  [31:0] in_2,
  input  [2:0] in_3,
  input  [31:0] in_4,
  input  [31:0] in_5,
  input  [31:0] in_6,
  input  [31:0] in_7,
  input  in_8,
  input  [4:0] in_9,
  input  in_10,
  input  in_11,
  input  [4:0] in_12,
  input  in_13,
  input  in_14,
  input  in_15,
  input  [4:0] in_16,
  output [31:0] SP,
  output [31:0] out_18,
  output [31:0] out_19
);

  wire and_1_out, and_2_out, and_3_out, and_4_out, and_5_out, and_6_out, and_7_out, and_8_out, and_9_out,
       and_10_out, and_11_out, and_12_out, and_13_out, and_14_out, and_15_out, and_16_out, and_17_out,
       and_18_out, and_19_out, and_20_out, and_21_out, and_22_out, and_23_out, and_24_out, and_25_out,
       and_26_out, and_27_out, and_28_out, and_29_out, and_30_out, and_31_out, and_32_out, fstack, h1, h2,
       h3, h4, h5, h6, h7, h8, h9, h10, h11, h12, h13, h14, h15, h16, h17, h18, h19, h20, h21, h22, h23, h24,
       h25, h26, h27, h28, h29, h30, h31, h32, or_2_out;
  wire [31:0] adder_1_out, inp, o1, o2, o3, o4, o5, o6, o7, o8, o9, o10, o11, o12, o13, o14, o15, o16, o17,
       o18, o19, o20, o21, o22, o23, o24, o25, o26, o27, o28, o29, o30, o31, Sp_t, Stack, subtractor_1_out;

  Decoder #(.select(5), .enable("false")) decoder_1 (
    .out0(h1), .out1(h2), .out2(h3), .out3(h4), .out4(h5), .out5(h6), .out6(h7), .out7(h8), .out8(h9),
    .out9(h10), .out10(h11), .out11(h12), .out12(h13), .out13(h14), .out14(h15), .out15(h16), .out16(h17),
    .out17(h18), .out18(h19), .out19(h20), .out20(h21), .out21(h22), .out22(h23), .out23(h24), .out24(h25),
    .out25(h26), .out26(h27), .out27(h28), .out28(h29), .out29(h30), .out30(h31), .out31(h32), .sel(in_16));
  Multiplexer #(.select(3), .width(32), .enable("false")) multiplexer_1 (
    .in0(in_1), .in1(in_2), .in2(in_4), .in3(in_5), .in4(in_6), .in5(in_7), .out(inp), .sel(in_3));  // open: in6, in7
  Register #(.width(32)) register_1 (.D(inp), .en(and_1_out), .Q(o1), .clk(in_14), .clr(1'b1));
  and and_1 (and_1_out, h1, in_13);
  Register #(.width(32)) register_2 (.D(inp), .en(and_2_out), .Q(o2), .clk(in_14), .clr(in_15));
  and and_2 (and_2_out, h2, in_13);
  Register #(.width(32)) register_3 (.D(inp), .en(and_3_out), .Q(o3), .clk(in_14), .clr(in_15));
  and and_3 (and_3_out, h3, in_13);
  Register #(.width(32)) register_4 (.D(inp), .en(and_4_out), .Q(o4), .clk(in_14), .clr(in_15));
  and and_4 (and_4_out, h4, in_13);
  Register #(.width(32)) register_5 (.D(inp), .en(and_5_out), .Q(o5), .clk(in_14), .clr(in_15));
  and and_5 (and_5_out, h5, in_13);
  Register #(.width(32)) register_6 (.D(inp), .en(and_6_out), .Q(o6), .clk(in_14), .clr(in_15));
  and and_6 (and_6_out, h6, in_13);
  Register #(.width(32)) register_7 (.D(inp), .en(and_7_out), .Q(o7), .clk(in_14), .clr(in_15));
  and and_7 (and_7_out, h7, in_13);
  Register #(.width(32)) register_8 (.D(inp), .en(and_8_out), .Q(o8), .clk(in_14), .clr(in_15));
  and and_8 (and_8_out, h8, in_13);
  Register #(.width(32)) register_9 (.D(inp), .en(and_9_out), .Q(o9), .clk(in_14), .clr(in_15));
  and and_9 (and_9_out, h9, in_13);
  Register #(.width(32)) register_10 (.D(inp), .en(and_10_out), .Q(o10), .clk(in_14), .clr(in_15));
  and and_10 (and_10_out, h10, in_13);
  Register #(.width(32)) register_11 (.D(inp), .en(and_11_out), .Q(o11), .clk(in_14), .clr(in_15));
  and and_11 (and_11_out, h11, in_13);
  Register #(.width(32)) register_12 (.D(inp), .en(and_12_out), .Q(o12), .clk(in_14), .clr(in_15));
  and and_12 (and_12_out, h12, in_13);
  Register #(.width(32)) register_13 (.D(inp), .en(and_13_out), .Q(o13), .clk(in_14), .clr(in_15));
  and and_13 (and_13_out, h13, in_13);
  Register #(.width(32)) register_14 (.D(inp), .en(and_14_out), .Q(o14), .clk(in_14), .clr(in_15));
  and and_14 (and_14_out, h14, in_13);
  Register #(.width(32)) register_15 (.D(inp), .en(and_15_out), .Q(o15), .clk(in_14), .clr(in_15));
  and and_15 (and_15_out, h15, in_13);
  Register #(.width(32)) register_16 (.D(inp), .en(and_16_out), .Q(o16), .clk(in_14), .clr(in_15));
  and and_16 (and_16_out, h16, in_13);
  Register #(.width(32)) register_17 (.D(inp), .en(and_17_out), .Q(o17), .clk(in_14), .clr(in_15));
  and and_17 (and_17_out, h17, in_13);
  Register #(.width(32)) register_18 (.D(inp), .en(and_18_out), .Q(o18), .clk(in_14), .clr(in_15));
  and and_18 (and_18_out, h18, in_13);
  Register #(.width(32)) register_19 (.D(inp), .en(and_19_out), .Q(o19), .clk(in_14), .clr(in_15));
  and and_19 (and_19_out, h19, in_13);
  Register #(.width(32)) register_20 (.D(inp), .en(and_20_out), .Q(o20), .clk(in_14), .clr(in_15));
  and and_20 (and_20_out, h20, in_13);
  and and_21 (and_21_out, h21, in_13);
  and and_22 (and_22_out, h22, in_13);
  and and_23 (and_23_out, h23, in_13);
  and and_24 (and_24_out, h24, in_13);
  and and_25 (and_25_out, h25, in_13);
  and and_26 (and_26_out, h26, in_13);
  and and_27 (and_27_out, h27, in_13);
  and and_28 (and_28_out, h28, in_13);
  and and_29 (and_29_out, h29, in_13);
  and and_30 (and_30_out, h30, in_13);
  Register #(.width(32)) register_21 (.D(inp), .en(and_21_out), .Q(o21), .clk(in_14), .clr(in_15));
  Register #(.width(32)) register_22 (.D(inp), .en(and_22_out), .Q(o22), .clk(in_14), .clr(in_15));
  Register #(.width(32)) register_23 (.D(inp), .en(and_23_out), .Q(o23), .clk(in_14), .clr(in_15));
  Register #(.width(32)) register_24 (.D(inp), .en(and_24_out), .Q(o24), .clk(in_14), .clr(in_15));
  Register #(.width(32)) register_25 (.D(inp), .en(and_25_out), .Q(o25), .clk(in_14), .clr(in_15));
  Register #(.width(32)) register_26 (.D(inp), .en(and_26_out), .Q(o26), .clk(in_14), .clr(in_15));
  Register #(.width(32)) register_27 (.D(inp), .en(and_27_out), .Q(o27), .clk(in_14), .clr(in_15));
  Register #(.width(32)) register_28 (.D(inp), .en(and_28_out), .Q(o28), .clk(in_14), .clr(in_15));
  Register #(.width(32)) register_29 (.D(inp), .en(and_29_out), .Q(o29), .clk(in_14), .clr(in_15));
  Register #(.width(32)) register_30 (.D(inp), .en(and_30_out), .Q(o30), .clk(in_14), .clr(in_15));
  Multiplexer #(.select(5), .width(32), .enable("false")) multiplexer_2 (
    .in0(o1), .in1(o2), .in2(o3), .in3(o4), .in4(o5), .in5(o6), .in6(o7), .in7(o8), .in8(o9), .in9(o10),
    .in10(o11), .in11(o12), .in12(o13), .in13(o14), .in14(o15), .in15(o16), .in16(o17), .in17(o18),
    .in18(o19), .in19(o20), .in20(o21), .in21(o22), .in22(o23), .in23(o24), .in24(o25), .in25(o26),
    .in26(o27), .in27(o28), .in28(o29), .in29(o30), .in30(o31), .in31(SP), .out(out_18), .sel(in_9));
  or or_1 (fstack, in_10, in_8);
  and and_31 (and_31_out, h31, in_13);
  or or_2 (or_2_out, in_11, and_32_out);
  and and_32 (and_32_out, h32, in_13);
  Multiplexer #(.select(5), .width(32), .enable("false")) multiplexer_3 (
    .in0(o1), .in1(o2), .in2(o3), .in3(o4), .in4(o5), .in5(o6), .in6(o7), .in7(o8), .in8(o9), .in9(o10),
    .in10(o11), .in11(o12), .in12(o13), .in13(o14), .in14(o15), .in15(o16), .in16(o17), .in17(o18),
    .in18(o19), .in19(o20), .in20(o21), .in21(o22), .in22(o23), .in23(o24), .in24(o25), .in25(o26),
    .in26(o27), .in27(o28), .in28(o29), .in29(o30), .in30(o31), .in31(SP), .out(out_19), .sel(in_12));
  Register #(.width(32)) register_31 (.D(inp), .en(and_31_out), .Q(o31), .clk(in_14), .clr(in_15));
  Register #(.width(32)) register_32 (.D(Sp_t), .en(or_2_out), .Q(SP), .clk(in_14), .clr(in_15));
  Adder #(.width(32)) adder_1 (.a(SP), .b(32'h4), .out(adder_1_out));  // open: cin, cout
  Subtractor #(.width(32)) subtractor_1 (.a(SP), .b(32'h4), .out(subtractor_1_out));  // open: bin, bout
  Multiplexer #(.width(32), .enable("false")) multiplexer_4 (
    .in0(adder_1_out), .in1(subtractor_1_out), .out(Stack), .sel(in_8));
  Multiplexer #(.width(32), .enable("false")) multiplexer_5 (.in0(inp), .in1(Stack), .out(Sp_t), .sel(fstack));

  // Other names for the same wires on the sheet: a[31:0] = out_18; able = in_13; b[31:0] = out_19; c = in_14;
  //   chsp = in_11; HI[31:0] = in_6; KBDATA[31:0] = in_5; Lo[31:0] = in_7; o32[31:0] = SP; pop = in_10; push = in_8;
  //   R[31:0] = in_1; r_t = in_15; RK[31:0] = in_2; Rout[31:0] = in_4
endmodule

module ALU (
  input  [31:0] in_1,
  input  [31:0] in_2,
  input  [3:0] in_3,
  output [31:0] out_4,
  output [31:0] out_5,
  output out_6,
  output out_7
);

  wire adder_1_cout, comparator_1_lt, comparator_2_lt, subtractor_1_bout;
  wire [31:0] c_minus, c_plus, c_star, c_u, o, o_minus, o_plus, o_star, o_t, o_u, o_u_t, o_u_t_t, oand, onor,
       oor, oxor, slt, sltu;

  assign oand = in_1 & in_2;  // AND_Gate and_1, 32 bits wide
  assign oor = in_1 | in_2;  // OR_Gate or_1, 32 bits wide
  assign onor = ~(in_1 | in_2);  // NOR_Gate nor_1, 32 bits wide
  assign oxor = in_1 ^ in_2;  // XOR_Gate xor_1, 32 bits wide
  Adder #(.width(32)) adder_1 (.a(in_1), .b(in_2), .out(o_plus), .cout(adder_1_cout));  // open: cin
  Subtractor #(.width(32)) subtractor_1 (.a(in_1), .b(in_2), .out(o_minus), .bout(subtractor_1_bout));  // open: bin
  Multiplier #(.width(32)) multiplier_1 (.a(in_1), .b(in_2), .out(o_star), .cout(c_star));  // open: cin
  Mulu mulu_1 (.A(in_1), .B(in_2), .Hi(o_u_t), .Lo(c_u));
  div div_1 (.DIVIDENDO(in_1), .DIVISOR(in_2), .COCIENTE(o_t), .RESTO(o));
  Divider #(.width(32)) divider_1 (.a(in_1), .b(in_2), .out(o_u_t_t), .rem(o_u));  // open: upper
  Comparator #(.width(32)) comparator_1 (.a(in_1), .b(in_2), .lt(comparator_1_lt));  // open: gt, eq
  assign slt = {{31{1'b0}}, comparator_1_lt};  // Bit_Extender bit_extender_1
  Comparator #(.width(32), .mode("unsigned")) comparator_2 (.a(in_1), .b(in_2), .lt(comparator_2_lt));  // open: gt, eq
  assign sltu = {{31{1'b0}}, comparator_2_lt};  // Bit_Extender bit_extender_2
  assign c_plus = {{31{1'b0}}, adder_1_cout};  // Bit_Extender bit_extender_3
  assign c_minus = {{31{1'b0}}, subtractor_1_bout};  // Bit_Extender bit_extender_4
  Multiplexer #(.select(4), .width(32), .enable("false")) multiplexer_1 (
    .in0(o_plus), .in1(o_minus), .in2(o_star), .in3(c_u), .in4(o_t), .in5(o_u_t_t), .in6(oand), .in7(oor),
    .in8(oxor), .in9(onor), .in10(slt), .in11(sltu), .out(out_5), .sel(in_3));  // open: in12, in13, in14, in15
  Multiplexer #(.select(4), .width(32), .enable("false")) multiplexer_2 (
    .in0(c_plus), .in1(c_minus), .in2(c_star), .in3(o_u_t), .in4(o), .in5(o_u), .in6({32{1'b0}}),
    .in7({32{1'b0}}), .in8({32{1'b0}}), .in9({32{1'b0}}), .in10({32{1'b0}}), .in11({32{1'b0}}), .out(out_4),
    .sel(in_3));  // open: in12, in13, in14, in15
  Comparator #(.width(32)) comparator_3 (.a(out_5), .b({32{1'b0}}), .eq(out_6), .lt(out_7));  // open: gt

  // Other names for the same wires on the sheet: i1[31:0] = in_1; i2[31:0] = in_2; op[3:0] = in_3; rem[31:0] = out_4;
  //   res[31:0] = out_5
endmodule

module BC (
  input  [31:0] in_1,
  input  in_2,
  input  [31:0] in_3,
  input  [2:0] in_4,
  input  [31:0] in_5,
  input  in_6,
  input  in_7,
  input  [1:0] in_8,
  output [31:0] out_9
);

  wire a, and_2_out, and_3_out, and_4_out, and_5_out, and_6_out, f, l, o, s0, s1, s2, s3, s4, s5, s6, s7;
  wire [1:0] sel;
  wire [31:0] and_7_out, and_8_out, js, mul, res, rp, sum;

  Decoder #(.select(3), .enable("false")) decoder_1 (
    .out0(s0), .out1(s1), .out2(s2), .out3(s3), .out4(s4), .out5(s5), .out6(s6), .out7(s7), .sel(in_4));
  Multiplexer #(.width(32), .enable("false")) multiplexer_1 (.in0(in_1), .in1(in_3), .out(js), .sel(in_2));
  or or_1 (o, in_6, in_7);
  and and_1 (a, ~in_6, ~in_7);  // AND_Gate
  en en_1 (.i0(s0), .i1(l), .i2(s6), .i3(s7), .o0(sel[0]), .o1(sel[1]));
  and and_2 (and_2_out, s1, f);
  and and_3 (and_3_out, s2, ~f);  // AND_Gate
  and and_4 (and_4_out, s3, f);
  and and_5 (and_5_out, s4, f);
  and and_6 (and_6_out, s5, f);
  Multiplexer #(.select(2), .enable("false")) multiplexer_2 (
    .in0(in_6), .in1(in_7), .in2(o), .in3(a), .out(f), .sel(in_8));
  or or_2 (l, and_2_out, and_3_out, and_4_out, and_5_out, and_6_out);
  Adder #(.width(32)) adder_1 (.a(in_5), .b(32'h4), .out(sum));  // open: cin, cout
  Multiplier #(.width(32)) multiplier_1 (.a(js), .b(32'h4), .out(mul));  // open: cin, cout
  Adder #(.width(32)) adder_2 (.a(sum), .b(mul), .out(res));  // open: cin, cout
  assign and_7_out = in_5 & 32'hf0000000;  // AND_Gate and_7, 32 bits wide
  assign and_8_out = mul & 32'hfffffff;  // AND_Gate and_8, 32 bits wide
  assign rp = and_7_out | and_8_out;  // OR_Gate or_3, 32 bits wide
  Multiplexer #(.select(2), .width(32), .enable("false")) multiplexer_3 (
    .in0(sum), .in1(res), .in2(rp), .in3(js), .out(out_9), .sel(sel));

  // Other names for the same wires on the sheet: _0 = in_6; ii[31:0] = in_5; N = in_7
endmodule

module en (
  input  i0,
  input  i1,
  input  i2,
  input  i3,
  output o0,
  output o1
);

  wire and_1_out, not_1_out;

  and and_1 (and_1_out, i1, not_1_out);
  not not_1 (not_1_out, i2);
  or or_1 (o1, i3, i2);
  or or_2 (o0, i3, and_1_out);
endmodule

module INS_DEC (
  input  [31:0] in_1,
  output [31:0] K,
  output [4:0] Sa,
  output [4:0] Sb,
  output [4:0] DA,
  output [2:0] DS,
  output [2:0] Jump,
  output [1:0] FC,
  output OS,
  output Mul_Div,
  output Op_const,
  output pop,
  output push,
  output nop,
  output halt,
  output tty,
  output rnd,
  output kbd,
  output [3:0] Op,
  output alu,
  output wrf,
  output lw,
  output sw
);

  wire add, addi, \and , and_30_out, and_41_out, and_42_out, andi, beq, bgtz, blez, bltz, bnq, div, divu,
       ins__i, ins__j, ins__r, k1, k2, mfhi, mflo, mult, mulu, \nor , opand, opor, opslt, opsltu, opsub,
       opxor, \or , ori, R_espec, R_pila, R_simple, Rout, Rrs, slt, slti, sltiu, sltu, sub, \xor , xori;
  wire [1:0] selk;

  or or_1 (ins__r, R_espec, R_simple, R_pila);
  and and_1 (R_espec, in_1[26], in_1[27], in_1[28], in_1[29], in_1[30], in_1[31]);
  and and_2 (R_simple, ~in_1[26], ~in_1[27], ~in_1[28], ~in_1[29], ~in_1[30], ~in_1[31]);  // AND_Gate
  and and_3 (R_pila, ~in_1[26], ~in_1[27], ~in_1[28], in_1[29], in_1[30], in_1[31]);  // AND_Gate
  and and_4 (nop, ~in_1[0], ~in_1[1], ~in_1[2], ~in_1[3], ~in_1[4], ~in_1[5], R_simple);  // AND_Gate
  and and_5 (add, ~in_1[0], ~in_1[1], ~in_1[2], ~in_1[3], ~in_1[4], in_1[5], R_simple);  // AND_Gate
  nor nor_1 (ins__i, ins__j, ins__r);
  and and_6 (ins__j, ~in_1[26], in_1[27], ~in_1[28], ~in_1[29], ~in_1[30], ~in_1[31]);  // AND_Gate
  and and_7 (sub, ~in_1[0], in_1[1], ~in_1[2], ~in_1[3], ~in_1[4], in_1[5], R_simple);  // AND_Gate
  and and_8 (mult, ~in_1[0], ~in_1[1], ~in_1[2], in_1[3], in_1[4], ~in_1[5], R_simple);  // AND_Gate
  en en_1 (.i1(k1), .i2(k2), .i3(ins__j), .o0(selk[0]), .o1(selk[1]));  // open: i0
  and and_9 (addi, ~in_1[26], ~in_1[27], ~in_1[28], in_1[29], ~in_1[30], ~in_1[31], ins__i);  // AND_Gate
  and and_10 (slti, ~in_1[26], in_1[27], ~in_1[28], in_1[29], ~in_1[30], ~in_1[31], ins__i);  // AND_Gate
  and and_11 (push, R_pila, in_1[0]);
  and and_12 (mulu, in_1[0], ~in_1[1], ~in_1[2], in_1[3], in_1[4], ~in_1[5], R_simple);  // AND_Gate
  and and_13 (div, ~in_1[0], in_1[1], ~in_1[2], in_1[3], in_1[4], ~in_1[5], R_simple);  // AND_Gate
  and and_14 (sltiu, in_1[26], in_1[27], ~in_1[28], in_1[29], ~in_1[30], ~in_1[31], ins__i);  // AND_Gate
  and and_15 (andi, ~in_1[26], ~in_1[27], in_1[28], in_1[29], ~in_1[30], ~in_1[31], ins__i);  // AND_Gate
  and and_16 (pop, ~in_1[0], R_pila);  // AND_Gate
  and and_17 (divu, in_1[0], in_1[1], ~in_1[2], in_1[3], in_1[4], ~in_1[5], R_simple);  // AND_Gate
  and and_18 (slt, ~in_1[0], in_1[1], ~in_1[2], in_1[3], ~in_1[4], in_1[5], R_simple);  // AND_Gate
  or or_2 (k1, sw, bnq, beq, bltz, lw, blez, bgtz, slti, sltiu, addi);
  or or_3 (opsub, sub, beq, bnq);
  or or_4 (opand, \and , andi);
  or or_5 (opsltu, sltiu, sltu);
  and and_19 (ori, in_1[26], ~in_1[27], in_1[28], in_1[29], ~in_1[30], ~in_1[31], ins__i);  // AND_Gate
  and and_20 (xori, ~in_1[26], in_1[27], in_1[28], in_1[29], ~in_1[30], ~in_1[31], ins__i);  // AND_Gate
  and and_21 (bltz, in_1[26], ~in_1[27], ~in_1[28], ~in_1[29], ~in_1[30], ~in_1[31], ins__i);  // AND_Gate
  and and_22 (sltu, in_1[0], in_1[1], ~in_1[2], in_1[3], ~in_1[4], in_1[5], R_simple);  // AND_Gate
  and and_23 (\and , ~in_1[0], ~in_1[1], in_1[2], ~in_1[3], ~in_1[4], in_1[5], R_simple);  // AND_Gate
  and and_24 (kbd, ~in_1[0], ~in_1[1], in_1[2], R_espec);  // AND_Gate
  and and_25 (lw, in_1[26], in_1[27], ~in_1[28], ~in_1[29], ~in_1[30], in_1[31], ins__i);  // AND_Gate
  and and_26 (sw, in_1[26], in_1[27], ~in_1[28], in_1[29], ~in_1[30], in_1[31], ins__i);  // AND_Gate
  or or_6 (k2, andi, xori, ori);
  or or_7 (opor, \or , ori, blez, bgtz, bltz);
  or or_8 (opxor, \xor , xori);
  or or_9 (opslt, slt, slti);
  and and_27 (\or , in_1[0], ~in_1[1], in_1[2], ~in_1[3], ~in_1[4], in_1[5], R_simple);  // AND_Gate
  and and_28 (\nor , in_1[0], in_1[1], in_1[2], ~in_1[3], ~in_1[4], in_1[5], R_simple);  // AND_Gate
  and and_29 (halt, in_1[0], in_1[1], in_1[2], R_espec);
  and and_30 (and_30_out, R_simple, ~Mul_Div, ~nop, ~OS);  // AND_Gate
  and and_31 (beq, ~in_1[26], ~in_1[27], in_1[28], ~in_1[29], ~in_1[30], ~in_1[31], ins__i);  // AND_Gate
  and and_32 (bnq, in_1[26], ~in_1[27], in_1[28], ~in_1[29], ~in_1[30], ~in_1[31], ins__i);  // AND_Gate
  and and_33 (tty, in_1[0], ~in_1[1], ~in_1[2], R_espec);  // AND_Gate
  and and_34 (\xor , ~in_1[0], ~in_1[1], ~in_1[2], in_1[3], ~in_1[4], in_1[5], R_simple);  // AND_Gate
  and and_35 (OS, ~in_1[0], ~in_1[1], ~in_1[2], in_1[3], ~in_1[4], ~in_1[5], R_simple);  // AND_Gate
  or or_10 (Rrs, blez, bltz, bgtz);
  or or_11 (Mul_Div, div, mult, mulu, divu);
  or or_12 (wrf, and_30_out, andi, ori, xori, slti, lw, sltiu, pop, rnd, kbd, addi);
  and and_36 (mfhi, ~in_1[0], ~in_1[1], ~in_1[2], ~in_1[3], in_1[4], ~in_1[5], R_simple);  // AND_Gate
  and and_37 (mflo, ~in_1[0], in_1[1], ~in_1[2], ~in_1[3], in_1[4], ~in_1[5], R_simple);  // AND_Gate
  and and_38 (blez, ~in_1[26], in_1[27], in_1[28], ~in_1[29], ~in_1[30], ~in_1[31], ins__i);  // AND_Gate
  and and_39 (bgtz, in_1[26], in_1[27], in_1[28], ~in_1[29], ~in_1[30], ~in_1[31], ins__i);  // AND_Gate
  and and_40 (rnd, ~in_1[0], in_1[1], ~in_1[2], R_espec);  // AND_Gate
  or or_13 (Rout, lw, pop);
  Multiplexer #(.select(2), .width(32), .enable("false")) multiplexer_1 (
    .in0({32{1'b0}}), .in1({{17{in_1[15]}}, in_1[14:0]}), .in2({{16{1'b0}}, in_1[15:0]}),
    .in3({{7{in_1[25]}}, in_1[24:0]}), .out(K), .sel(selk));
  Multiplexer #(.width(5), .enable("false")) multiplexer_2 (.in0(in_1[20:16]), .in1(in_1[25:21]), .out(Sb), .sel(Rrs));
  Multiplexer #(.width(5), .enable("false")) multiplexer_3 (
    .in0(in_1[15:11]), .in1(in_1[20:16]), .out(DA), .sel(ins__i));
  Priority_Encoder priority_encoder_1 (
    .in0(1'b1), .in1(rnd), .in2(Rout), .in3(kbd), .in4(mfhi), .in5(mflo), .out(DS), .en_in(1'b1));  // open: in6, in7, gs, en_out
  or or_14 (Op_const, sltiu, addi, andi, slti, ori, xori);
  Priority_Encoder #(.select(4)) priority_encoder_2 (
    .in0(1'b1), .in1(opsub), .in2(mult), .in3(mulu), .in4(div), .in5(divu), .in6(opand), .in7(opor),
    .in8(opxor), .in9(\nor ), .in10(opslt), .in11(opsltu), .out(Op), .en_in(1'b1));  // open: in12, in13, in14, in15, gs, en_out
  and and_41 (and_41_out, R_simple, ~nop, ~OS, ~mfhi, ~mflo);  // AND_Gate
  and and_42 (and_42_out, ins__i, ~lw, ~sw);  // AND_Gate
  Priority_Encoder priority_encoder_3 (
    .in0(1'b1), .in1(beq), .in2(bnq), .in3(blez), .in4(bgtz), .in5(bltz), .in6(ins__j), .in7(OS), .out(Jump),
    .en_in(1'b1));  // open: gs, en_out
  Priority_Encoder #(.select(2)) priority_encoder_4 (
    .in0(1'b1), .in1(bltz), .in2(blez), .in3(bgtz), .out(FC), .en_in(1'b1));  // open: gs, en_out
  or or_15 (alu, and_41_out, and_42_out);

  assign Sa = in_1[25:21];

  // Other names for the same wires on the sheet: Const[15:0] = in_1[15:0];
  //   Const1[31:0] = {{17{in_1[15]}}, in_1[14:0]}; Const2[15:0] = in_1[15:0];
  //   const3[31:0] = {{7{in_1[25]}}, in_1[24:0]}; Destino[25:0] = in_1[25:0]; f1 = in_1[0]; funct[5:0] = in_1[5:0];
  //   f2 = in_1[1]; f3 = in_1[2]; f4 = in_1[3]; f5 = in_1[4]; f6 = in_1[5]; jr = OS; muldiv = Mul_Div; o1 = in_1[26];
  //   Op_code[5:0] = in_1[31:26]; o2 = in_1[27]; o3 = in_1[28]; o4 = in_1[29]; o5 = in_1[30]; o6 = in_1[31];
  //   Rd[4:0] = in_1[15:11]; Rs[4:0] = in_1[25:21]; Rt[4:0] = in_1[20:16]
endmodule

module div (
  input  [31:0] DIVIDENDO,
  input  [31:0] DIVISOR,
  output [31:0] COCIENTE,
  output [31:0] RESTO
);

  wire xor_1_out;
  wire [31:0] adder_1_out, C, not_42_out, not_63_out, RESTO_t;

  not not_1 (not_42_out[30], RESTO_t[30]);
  not not_2 (not_42_out[29], RESTO_t[29]);
  not not_3 (not_42_out[27], RESTO_t[27]);
  not not_4 (not_42_out[28], RESTO_t[28]);
  not not_5 (not_42_out[31], RESTO_t[31]);
  Divider #(.width(32)) divider_1 (.a(DIVIDENDO), .b(DIVISOR), .out(C), .rem(RESTO_t));  // open: upper
  not not_6 (not_42_out[20], RESTO_t[20]);
  not not_7 (not_42_out[26], RESTO_t[26]);
  not not_8 (not_42_out[21], RESTO_t[21]);
  not not_9 (not_42_out[19], RESTO_t[19]);
  not not_10 (not_42_out[22], RESTO_t[22]);
  not not_11 (not_42_out[25], RESTO_t[25]);
  not not_12 (not_42_out[23], RESTO_t[23]);
  not not_13 (not_42_out[24], RESTO_t[24]);
  not not_14 (not_42_out[18], RESTO_t[18]);
  not not_15 (not_42_out[12], RESTO_t[12]);
  not not_16 (not_42_out[16], RESTO_t[16]);
  not not_17 (not_42_out[17], RESTO_t[17]);
  not not_18 (not_42_out[14], RESTO_t[14]);
  not not_19 (not_42_out[15], RESTO_t[15]);
  not not_20 (not_42_out[13], RESTO_t[13]);
  not not_21 (not_42_out[11], RESTO_t[11]);
  not not_22 (not_63_out[31], C[31]);
  not not_23 (not_63_out[30], C[30]);
  not not_24 (not_63_out[28], C[28]);
  not not_25 (not_63_out[29], C[29]);
  not not_26 (not_42_out[3], RESTO_t[3]);
  not not_27 (not_42_out[4], RESTO_t[4]);
  not not_28 (not_42_out[9], RESTO_t[9]);
  not not_29 (not_42_out[8], RESTO_t[8]);
  not not_30 (not_42_out[5], RESTO_t[5]);
  not not_31 (not_42_out[10], RESTO_t[10]);
  not not_32 (not_42_out[6], RESTO_t[6]);
  not not_33 (not_42_out[7], RESTO_t[7]);
  not not_34 (not_63_out[22], C[22]);
  not not_35 (not_63_out[23], C[23]);
  not not_36 (not_63_out[24], C[24]);
  not not_37 (not_63_out[21], C[21]);
  not not_38 (not_63_out[26], C[26]);
  not not_39 (not_63_out[20], C[20]);
  not not_40 (not_63_out[25], C[25]);
  not not_41 (not_63_out[27], C[27]);
  not not_42 (not_42_out[0], RESTO_t[0]);
  not not_43 (not_42_out[2], RESTO_t[2]);
  not not_44 (not_42_out[1], RESTO_t[1]);
  not not_45 (not_63_out[14], C[14]);
  not not_46 (not_63_out[16], C[16]);
  not not_47 (not_63_out[18], C[18]);
  not not_48 (not_63_out[17], C[17]);
  not not_49 (not_63_out[13], C[13]);
  not not_50 (not_63_out[19], C[19]);
  not not_51 (not_63_out[15], C[15]);
  not not_52 (not_63_out[12], C[12]);
  Multiplexer #(.width(32), .enable("false")) multiplexer_1 (
    .in0(RESTO_t), .in1(not_42_out), .out(RESTO), .sel(DIVIDENDO[31]));
  not not_53 (not_63_out[8], C[8]);
  not not_54 (not_63_out[7], C[7]);
  not not_55 (not_63_out[9], C[9]);
  not not_56 (not_63_out[5], C[5]);
  not not_57 (not_63_out[4], C[4]);
  not not_58 (not_63_out[6], C[6]);
  not not_59 (not_63_out[11], C[11]);
  not not_60 (not_63_out[10], C[10]);
  not not_61 (not_63_out[1], C[1]);
  not not_62 (not_63_out[3], C[3]);
  not not_63 (not_63_out[0], C[0]);
  not not_64 (not_63_out[2], C[2]);
  Adder #(.width(32)) adder_1 (.a(not_63_out), .b(32'h1), .out(adder_1_out));  // open: cin, cout
  xor xor_1 (xor_1_out, DIVIDENDO[31], DIVISOR[31]);
  Multiplexer #(.width(32), .enable("false")) multiplexer_2 (
    .in0(C), .in1(adder_1_out), .out(COCIENTE), .sel(xor_1_out));

  // Other names for the same wires on the sheet: A[31:0] = DIVIDENDO; SA = DIVIDENDO[31]; B[31:0] = DIVISOR;
  //   SB = DIVISOR[31]
endmodule

module Mulu (
  input  [31:0] A,
  input  [31:0] B,
  output [31:0] Hi,
  output [31:0] Lo
);

  wire adder_1_cout, adder_3_cout, adder_5_cout, adder_8_cout, ps;
  wire [0:0] multiplexer_1_out, multiplexer_2_out;
  wire [1:0] Hi1;
  wire [29:0] Lo0;
  wire [30:0] A1, B1;
  wire [31:0] adder_2_out, adder_3_out, adder_6_out, adder_9_out, Hi0, HiImp, HiParA, HiParB, LoImp, LoParA,
       LoParB, multiplexer_3_out, multiplexer_4_out, remp, resp, subtractor_1_out, subtractor_2_out;

  Multiplier #(.width(32)) multiplier_1 (.a(A), .b(B), .out(resp), .cout(remp));  // open: cin
  Multiplier #(.width(32)) multiplier_2 (.a({1'b0, A1}), .b({1'b0, B1}), .out({Hi1, Lo0}), .cout(Hi0));  // open: cin
  Adder #(.width(32)) adder_1 (.a({Lo0, 2'b00}), .b({A1, 1'b0}), .out(LoParB), .cout(adder_1_cout));  // open: cin
  Adder #(.width(32)) adder_2 (.a({Hi0[29:0], Hi1}), .b({32{1'b0}}), .out(adder_2_out));  // open: cin, cout
  Adder #(.width(32)) adder_3 (.a({B1, 1'b0}), .b(LoParB), .out(adder_3_out), .cout(adder_3_cout));  // open: cin
  Adder #(.width(32)) adder_4 (.a({32{1'b0}}), .b(adder_2_out), .out(HiParB), .cin(adder_1_cout));  // open: cout
  nor nor_1 (ps, A[31], B[31]);
  Adder #(.width(32)) adder_5 (.a(adder_3_out), .b(32'h1), .out(LoImp), .cout(adder_5_cout));  // open: cin
  Adder #(.width(32)) adder_6 (.a(HiParB), .b({32{1'b0}}), .out(adder_6_out), .cin(adder_3_cout));  // open: cout
  Subtractor #(.width(32)) subtractor_1 (.a(32'h1), .b(B), .out(subtractor_1_out));  // open: bin, bout
  Adder #(.width(32)) adder_7 (.a({32{1'b0}}), .b(adder_6_out), .out(HiImp), .cin(adder_5_cout));  // open: cout
  Multiplexer #(.width(32), .enable("false")) multiplexer_1 (
    .in0(A), .in1(subtractor_2_out), .out({A1, multiplexer_1_out[0]}), .sel(A[0]));
  Subtractor #(.width(32)) subtractor_2 (.a(32'h1), .b(A), .out(subtractor_2_out));  // open: bin, bout
  Multiplexer #(.width(32), .enable("false")) multiplexer_2 (
    .in0(B), .in1(subtractor_1_out), .out({B1, multiplexer_2_out[0]}), .sel(B[0]));
  Adder #(.width(32)) adder_8 (.a({Lo0, 2'b00}), .b({B1, 1'b0}), .out(LoParA), .cout(adder_8_cout));  // open: cin
  Adder #(.width(32)) adder_9 (.a({Hi0[29:0], Hi1}), .b({32{1'b0}}), .out(adder_9_out));  // open: cin, cout
  Adder #(.width(32)) adder_10 (.a({32{1'b0}}), .b(adder_9_out), .out(HiParA), .cin(adder_8_cout));  // open: cout
  Multiplexer #(.select(2), .width(32), .enable("false")) multiplexer_3 (
    .in0({Hi0[29:0], Hi1}), .in1(HiParA), .in2(HiParB), .in3(HiImp), .out(multiplexer_3_out),
    .sel({B[0], A[0]}));
  Multiplexer #(.select(2), .width(32), .enable("false")) multiplexer_4 (
    .in0({Lo0, 2'b00}), .in1(LoParA), .in2(LoParB), .in3(LoImp), .out(multiplexer_4_out), .sel({B[0], A[0]}));
  Multiplexer #(.width(32), .enable("false")) multiplexer_5 (.in0(multiplexer_3_out), .in1(remp), .out(Hi), .sel(ps));
  Multiplexer #(.width(32), .enable("false")) multiplexer_6 (.in0(multiplexer_4_out), .in1(resp), .out(Lo), .sel(ps));

  // Other names for the same wires on the sheet: AP = A[0]; BP = B[0]; nega = A[31]; A2Lo[31:1] = A1; negb = B[31];
  //   B2Lo[31:1] = B1; Hi1[31:2] = Hi0[29:0]; Lo0[31:30] = Hi1; Lo1[31:2] = Lo0
endmodule

module LE (
  input  [31:0] Input,
  output [31:0] out_2
);


  assign out_2 = {Input[7:0], Input[15:8], Input[23:16], Input[31:24]};
endmodule

module Waiter (
  input  CLK,
  input  [3:0] STOP,
  input  Reset,
  output Ouput
);

  wire comparator_1_lt, demultiplexer_1_out0;
  wire [3:0] counter_1_q;

  Counter #(.width(4), .max('hf)) counter_1 (
    .Q(counter_1_q), .clk(demultiplexer_1_out0), .clr(Reset));  // open: load, D, count, carry
  Comparator #(.width(4)) comparator_1 (.a(STOP), .b(counter_1_q), .lt(comparator_1_lt));  // open: gt, eq
  Demultiplexer #(.enable("false")) demultiplexer_1 (
    .out0(demultiplexer_1_out0), .out1(Ouput), .in(CLK), .sel(comparator_1_lt));
endmodule

module RAM_Dispatcher (
  input  [3:0] WriteTime,
  input  Clock,
  input  CLR,
  output [31:0] Data,
  output [15:0] Address,
  output [3:0] Mask,
  output Finished,
  output Write
);

  wire demultiplexer_2_out1, demultiplexer_3_out1, End, IDLE_q, IncAddr, Load, or_1_out, or_2_out, While_q,
       WriteEnd;
  wire [3:0] counter_1_q;
  wire [31:0] CurrentAddress_q;

  Counter #(.width(32), .max('hffffffff)) CurrentAddress (
    .count(IncAddr), .Q({CurrentAddress_q[31:18], Address, CurrentAddress_q[1:0]}), .clk(Clock), .clr(CLR));  // open: load, D, carry
  or or_1 (or_1_out, IncAddr, demultiplexer_3_out1, Finished);
  D_Flip_Flop IDLE (.clk(Clock), .D(or_1_out), .Q(IDLE_q), .preset(CLR));  // open: Qn, en, reset
  Demultiplexer #(.enable("false")) demultiplexer_1 (.out0(Load), .out1(Finished), .in(IDLE_q), .sel(End));
  D_Flip_Flop While (.clk(Clock), .D(or_2_out), .Q(While_q), .reset(CLR));  // open: Qn, preset, en
  or or_2 (or_2_out, Write, Load);
  RAM_part #(.addrWidth(18), .dataWidth(32)) ram_1 (
    .addr({Address, CurrentAddress_q[1:0]}), .data(Data), .clk(Clock));  // open: sel, ld, clr
  Demultiplexer #(.enable("false")) demultiplexer_2 (
    .out0(Write), .out1(demultiplexer_2_out1), .in(While_q), .sel(WriteEnd));
  Decoder #(.select(2)) decoder_1 (
    .out0(Mask[0]), .out1(Mask[1]), .out2(Mask[2]), .out3(Mask[3]), .sel(CurrentAddress_q[1:0]));  // open: en
  Demultiplexer #(.enable("false")) demultiplexer_3 (
    .out0(IncAddr), .out1(demultiplexer_3_out1), .in(demultiplexer_2_out1), .sel(End));
  Counter #(.width(4), .max('hf)) counter_1 (
    .load(Load), .D(WriteTime), .count(Write), .Q(counter_1_q), .clk(Clock));  // open: carry, clr
  Comparator #(.width(32)) comparator_1 (.a(Data), .b({32{1'b1}}), .eq(End));  // open: gt, lt
  Comparator #(.width(4)) comparator_2 (.a(4'b0000), .b(counter_1_q), .eq(WriteEnd));  // open: gt, lt

  // Other names for the same wires on the sheet: CLK = Clock; Count = Write; WT[3:0] = WriteTime
endmodule
